# Fritzing sketch circuit12to5 (saved by Fritzing 0.9.3b)
breadboards: 1

parts:
  R1 = Resistor [tolerance=±5% resistance=560 package=THT]
  Q2 = npn-Powertransistor [package="TO220 [THT]"]
  U1 = TL431 [package="TO92 (Two)"]
  R2 = Resistor [tolerance=±5% resistance=10k package=THT]
  R3 = Resistor [tolerance=±5% resistance=10k package=THT]
  METER1 = 7-Segment Panel Voltmeter
  VM1 = Voltmeter (3 wire)
  C1 = Electrolytic Capacitor [capacitance=1µF package="100 mil [THT, electrolytic]"]

nets:
  N1: R1.Pin_0, Q2.collector, METER1.V+, METER1.V-
  N2: R1.Pin_1, Q2.base, U1.3
  VCC: Q2.emitter, R2.Pin_1, VM1.VCC, VM1.Vin, C1.+
  N3: U1.1, R2.Pin_0, R3.Pin_0
  N4: U1.2, R3.Pin_1, VM1.GND, C1.-

notes:
  上排輸入 7V~20V
  下排穩定 5V
  簡易 7V~20V 轉 5V
  By 羽山 https://3wa.tw
  470㎌/ 50V
  TIP41C
  560Ω
  10KΩ
  TL431

custom parts:
  TL431: 2% accuracy adjustable precision shunt regulator
  7-Segment Panel Voltmeter: 7-Segment Panel Voltmeter (4.5 - 30V)
  Voltmeter (3 wire): Voltmeter, 3 digit LED (.56 inch) output, 3 wire (Power 3.5V to 30V, Ground, Vin) comes in several colors (red, green, orange, blue). Available from Ebay and Amazon and others, no bezel (although bezels to fit them are currently available on Ebay). The mounting ears on what you get may or may not be the same as the ones I have. Won't run on 3.3V so you would need a 5 volt source or a 3V to 5V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
